# Fritzing sketch moduloBluetooth (saved by Fritzing 0.9.3b)

parts:
  Componente1 = Arduino Uno (Rev3) - ICSP
  Componente2 = Bluetooth HC-05 Macho
  K1 = Relay [part_number=FRS1B-S package=THT]
  K2 = Relay [part_number=FRS1B-S package=THT]

nets:
  N1: Componente1.D2, Componente2.TXD
  N2: Componente1.D3_PWM, Componente2.RXD
  5V: Componente1.5V, Componente2.VCC
  GND: Componente1.GND, Componente2.GND, K1.C1, K1.C2, K2.C2
